# Fritzing sketch Drum_Guitar_Hero (saved by Fritzing 1.0.4)
circuit board: 13.841cm x 9.34154cm
breadboards: 1

parts:
  Componente1 = Arduino Pro Micro (Clone)
  C1 = Ceramic Capacitor [capacitance=100nF voltage=35V package="100 mil [THT, multilayer]"]
  R1 = Resistor [tolerance=±5% power=0.25W resistance=1M package=THT]
  C2 = Electrolytic Capacitor [capacitance=100µF voltage=35V package="100 mil [THT, electrolytic]"]
  D1 = Zener Diode [part_number=1N4732A breakdown_voltage=3.6V package="Melf DO-213 AB [SMD]"]
  C3 = Ceramic Capacitor [capacitance=100nF voltage=35V package="100 mil [THT, multilayer]"]
  R2 = Resistor [tolerance=±5% power=0.25W resistance=1M package=THT]
  D3 = Zener Diode [part_number=1N4732A breakdown_voltage=3.6V package="Melf DO-213 AB [SMD]"]
  D4 = Zener Diode [part_number=1N4732A breakdown_voltage=3.6V package="Melf DO-213 AB [SMD]"]
  C4 = Ceramic Capacitor [capacitance=100nF voltage=35V package="100 mil [THT, multilayer]"]
  D5 = Zener Diode [part_number=1N4732A breakdown_voltage=3.6V package="Melf DO-213 AB [SMD]"]
  D6 = Zener Diode [part_number=1N4732A breakdown_voltage=3.6V package="Melf DO-213 AB [SMD]"]
  C5 = Ceramic Capacitor [capacitance=100nF voltage=35V package="100 mil [THT, multilayer]"]
  R4 = Resistor [tolerance=±5% power=0.25W resistance=1M package=THT]
  D7 = Zener Diode [part_number=1N4732A breakdown_voltage=3.6V package="Melf DO-213 AB [SMD]"]
  D8 = Zener Diode [part_number=1N4732A breakdown_voltage=3.6V package="Melf DO-213 AB [SMD]"]
  C6 = Ceramic Capacitor [capacitance=100nF voltage=35V package="100 mil [THT, multilayer]"]
  R5 = Resistor [tolerance=±5% power=0.25W resistance=1M package=THT]
  D9 = Zener Diode [part_number=1N4732A breakdown_voltage=3.6V package="Melf DO-213 AB [SMD]"]
  D10 = Zener Diode [part_number=1N4732A breakdown_voltage=3.6V package="Melf DO-213 AB [SMD]"]
  C7 = Ceramic Capacitor [capacitance=100nF voltage=35V package="100 mil [THT, multilayer]"]
  J1 = Piezo Speaker
  J2 = Piezo Speaker
  J3 = Piezo Speaker
  J4 = Piezo Speaker
  J5 = Piezo Speaker
  R6 = Resistor [tolerance=±5% power=0.25W resistance=2.2k package=THT]
  R7 = Resistor [tolerance=±5% power=0.25W resistance=2.2k package=THT]
  R8 = Resistor [tolerance=±5% power=0.25W resistance=2.2k package=THT]
  R9 = Resistor [tolerance=±5% power=0.25W resistance=2.2k package=THT]
  R10 = Resistor [tolerance=±5% power=0.25W resistance=2.2k package=THT]
  Componente2 = Analog Digital MUX Breakout
  D2 = Zener Diode [part_number=1N4732A breakdown_voltage=3.6V package="Melf DO-213 AB [SMD]"]
  R3 = Resistor [tolerance=±5% power=0.25W resistance=1M package=THT]

nets:
  N1: Componente1.GND, C1.0, C2.-, D1.anode, C3.1, D3.anode, C4.1, D5.anode, C5.1, D7.anode, C6.1, D9.anode, C7.1, J1.pin1, J2.pin1, J3.pin1, J4.pin1, J5.pin1
  N2: Componente1.D2, Componente2.S0
  N3: Componente1.D3, Componente2.S1
  N4: Componente1.D4, Componente2.S2
  N5: Componente1.D5, Componente2.S3
  N6: Componente1.A0, Componente2.SIG
  N7: Componente1.VCC, C1.1, C2.+, D4.cathode, D6.cathode, D8.cathode, D10.cathode, D2.cathode
  N8: R1.Pin_0, D1.cathode, C3.0, R6.Pin_1, Componente2.C0, D2.anode
  N9: R2.Pin_0, D3.cathode, D4.anode, C4.0, R7.Pin_1, Componente2.C1
  N10: D5.cathode, D6.anode, C5.0, R8.Pin_1, Componente2.C2, R3.Pin_0
  N11: R4.Pin_0, D7.cathode, D8.anode, C6.0, R9.Pin_1, Componente2.C3
  N12: R5.Pin_0, D9.cathode, D10.anode, C7.0, R10.Pin_1, Componente2.C4

custom parts:
  Analog Digital MUX Breakout: This is a breakout board for the very handy 16-Channel Analog/Digital Multiplexer/Demultiplexer CD74HC4067. This chip is like a rotary switch - it internally routes the common pin (COM in the schematic, SIG on the board) to one of 16 channel pins (CHANxx). It works with both digital and analog signals (the voltage can’t be higher than VCC), and the connections function in either direction. To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
